// Logisim project Xenia_C16V.circ as structural Verilog
module ALU (
  input  [15:0] A,
  input  [15:0] B,
  input  [3:0] OP
);
endmodule

module Half_Adder (
  input  A,
  input  B,
  output Carry,
  output Sum
);

  and and_1 (Carry, A, B);
  xor xor_1 (Sum, A, B);
endmodule

module Full_Adder (
  input  A,
  input  B,
  input  Carry_In,
  output Carry_Out,
  output Sum
);

  wire half_adder_1_carry, half_adder_1_sum, half_adder_2_carry;

  Half_Adder half_adder_1 (.A(A), .B(B), .Carry(half_adder_1_carry), .Sum(half_adder_1_sum));
  Half_Adder half_adder_2 (.A(half_adder_1_sum), .B(Carry_In), .Carry(half_adder_2_carry), .Sum(Sum));
  or or_1 (Carry_Out, half_adder_1_carry, half_adder_2_carry);
endmodule

module Full_Adder_8Bit (
  input  [7:0] A,
  input  [7:0] B,
  input  Carry_In,
  output [7:0] Sum,
  output Carry_Out
);

  wire full_adder_1_carry_out, full_adder_2_carry_out, full_adder_3_carry_out, full_adder_4_carry_out,
       full_adder_5_carry_out, full_adder_6_carry_out, full_adder_7_carry_out;

  Full_Adder full_adder_1 (.A(A[0]), .B(B[0]), .Carry_In(Carry_In), .Carry_Out(full_adder_1_carry_out), .Sum(Sum[0]));
  Full_Adder full_adder_2 (
    .A(A[1]), .B(B[1]), .Carry_In(full_adder_1_carry_out), .Carry_Out(full_adder_2_carry_out), .Sum(Sum[1]));
  Full_Adder full_adder_3 (
    .A(A[2]), .B(B[2]), .Carry_In(full_adder_2_carry_out), .Carry_Out(full_adder_3_carry_out), .Sum(Sum[2]));
  Full_Adder full_adder_4 (
    .A(A[3]), .B(B[3]), .Carry_In(full_adder_3_carry_out), .Carry_Out(full_adder_4_carry_out), .Sum(Sum[3]));
  Full_Adder full_adder_5 (
    .A(A[4]), .B(B[4]), .Carry_In(full_adder_4_carry_out), .Carry_Out(full_adder_5_carry_out), .Sum(Sum[4]));
  Full_Adder full_adder_6 (
    .A(A[5]), .B(B[5]), .Carry_In(full_adder_5_carry_out), .Carry_Out(full_adder_6_carry_out), .Sum(Sum[5]));
  Full_Adder full_adder_7 (
    .A(A[6]), .B(B[6]), .Carry_In(full_adder_6_carry_out), .Carry_Out(full_adder_7_carry_out), .Sum(Sum[6]));
  Full_Adder full_adder_8 (.A(A[7]), .B(B[7]), .Carry_In(full_adder_7_carry_out), .Carry_Out(Carry_Out), .Sum(Sum[7]));
endmodule
